# Fritzing sketch Standalone (saved by Fritzing 0.7.12b)
breadboards: 1

parts:
  XTAL2 = Crystal [frequency="16 Mhz" package=THT]
  C6 = Ceramic Capacitor [capacitance=100nF package="100 mil [THT, multilayer]"]
  C7 = Ceramic Capacitor [capacitance=100nF package="100 mil [THT, multilayer]"]
  U4 = Voltage Regulator - 5V [package="TO220 [THT]"]
  C8 = Electrolytic Capacitor [capacitance=10µF package="100 mil [THT, electrolytic]"]
  C9 = Electrolytic Capacitor [capacitance=10µF package="100 mil [THT, electrolytic]"]
  Power_plug2 = Power plug
  U3 = atmega328 [package=dip]

nets:
  N1: XTAL2.pin_0, C7.1, U3.XLAT1
  N2: XTAL2.pin_1, C6.1, U3.XLAT2
  GND: C6.0, C7.0, U4.GND, C8.-, C9.-, Power_plug2.GND, U3.GND
  N3: U4.input_voltage, C9.+, Power_plug2.VCC
  N4: U4.output_voltage, C8.+, U3.VCC, U3.AVCC, U3.AREF
